// Logisim project FPGA.circ as structural Verilog: 12 circuits, main circuit MotorController
module Pulser (
  input  Input,
  output Output
);


  assign Output = Input;
endmodule

// Pre.
module Prescaler (
  input  Reset,
  input  Clock,
  output PrescaledClock
);

  wire not_1_out;

  not not_1 (not_1_out, Reset);
  and and_1 (PrescaledClock, not_1_out, Clock);
endmodule

// Tim.
module Timer (
  input  Reset,
  input  Clock,
  output [7:0] Output
);

  Counter counter_1 (.count(1'b1), .Q(Output), .clk(Clock), .clr(Reset));  // open: load, D, carry
endmodule

// Enc.
module Encoder (
  input  Reset,
  input  Clock,
  input  [1:0] Input,
  output [7:0] Output
);
endmodule

// ENC\nCon.
module ENCController (
  input  Reset,
  input  ENCClock,
  input  [1:0] ENCInput,
  output [7:0] ENCTime,
  output [7:0] ENCVal
);

  wire prescaler_1_prescaledclock;

  Prescaler prescaler_1 (.Reset(Reset), .Clock(ENCClock), .PrescaledClock(prescaler_1_prescaledclock));
  Encoder encoder_1 (.Reset(Reset), .Clock(ENCClock), .Output(ENCVal), .Input(ENCInput));
  Timer timer_1 (.Reset(Reset), .Clock(prescaler_1_prescaledclock), .Output(ENCTime));
endmodule

module PWM (
  input  Reset,
  input  Clock,
  input  [6:0] CompareMatch,
  output Output
);

  wire [6:0] counter_1_q;

  Counter #(.width(7), .max('h7f)) counter_1 (
    .count(1'b1), .Q(counter_1_q), .clk(Clock), .clr(Reset));  // open: load, D, carry
  Comparator #(.width(7), .mode("unsigned")) comparator_1 (
    .a(counter_1_q), .b(CompareMatch), .lt(Output));  // open: gt, eq
endmodule

// PWM\nCon.
module PWMController (
  input  Reset,
  input  Clock,
  input  [7:0] PWMCompareMatch,
  output [1:0] PWMOutput
);

  wire not_3_out, prescaler_1_prescaledclock, pwm_1_output;
  wire [6:0] and_1_out, and_2_out, not_1_out, not_2_out, or_1_out;

  Prescaler prescaler_1 (.Reset(Reset), .Clock(Clock), .PrescaledClock(prescaler_1_prescaledclock));
  assign not_1_out = ~PWMCompareMatch[6:0];  // NOT_Gate not_1, 7 bits wide
  assign and_1_out = not_1_out & {7{PWMCompareMatch[7]}};  // AND_Gate and_1, 7 bits wide
  assign and_2_out = PWMCompareMatch[6:0] & not_2_out;  // AND_Gate and_2, 7 bits wide
  assign not_2_out = ~{7{PWMCompareMatch[7]}};  // NOT_Gate not_2, 7 bits wide
  PWM pwm_1 (.Reset(Reset), .Clock(prescaler_1_prescaledclock), .CompareMatch(or_1_out), .Output(pwm_1_output));
  not not_3 (not_3_out, PWMCompareMatch[7]);
  assign or_1_out = and_1_out | and_2_out;  // OR_Gate or_1, 7 bits wide
  and and_3 (PWMOutput[0], not_3_out, pwm_1_output);
  and and_4 (PWMOutput[1], pwm_1_output, PWMCompareMatch[7]);
endmodule

module SIPO (
  input  Reset,
  input  Clock,
  input  Latch,
  input  SerialInput,
  output [7:0] ParallelOutput,
  output ReadWrite
);

  wire and_1_out, d_ff_2_q, d_ff_4_q, d_ff_6_q, d_ff_8_q, d_ff_10_q, d_ff_13_q, d_ff_14_q, d_ff_16_q,
       d_ff_18_q, not_1_out;

  and and_1 (and_1_out, not_1_out, Latch);
  not not_1 (not_1_out, d_ff_18_q);
  D_Flip_Flop d_ff_1 (.clk(and_1_out), .D(d_ff_2_q), .Q(ParallelOutput[0]), .reset(Reset));  // open: Qn, preset, en
  D_Flip_Flop d_ff_2 (.clk(Clock), .D(SerialInput), .Q(d_ff_2_q), .reset(Reset));  // open: Qn, preset, en
  D_Flip_Flop d_ff_3 (.clk(and_1_out), .D(d_ff_4_q), .Q(ParallelOutput[1]), .reset(Reset));  // open: Qn, preset, en
  D_Flip_Flop d_ff_4 (.clk(Clock), .D(d_ff_2_q), .Q(d_ff_4_q), .reset(Reset));  // open: Qn, preset, en
  D_Flip_Flop d_ff_5 (.clk(and_1_out), .D(d_ff_6_q), .Q(ParallelOutput[2]), .reset(Reset));  // open: Qn, preset, en
  D_Flip_Flop d_ff_6 (.clk(Clock), .D(d_ff_4_q), .Q(d_ff_6_q), .reset(Reset));  // open: Qn, preset, en
  D_Flip_Flop d_ff_7 (.clk(and_1_out), .D(d_ff_8_q), .Q(ParallelOutput[3]), .reset(Reset));  // open: Qn, preset, en
  D_Flip_Flop d_ff_8 (.clk(Clock), .D(d_ff_6_q), .Q(d_ff_8_q), .reset(Reset));  // open: Qn, preset, en
  D_Flip_Flop d_ff_9 (.clk(and_1_out), .D(d_ff_10_q), .Q(ParallelOutput[4]), .reset(Reset));  // open: Qn, preset, en
  D_Flip_Flop d_ff_10 (.clk(Clock), .D(d_ff_8_q), .Q(d_ff_10_q), .reset(Reset));  // open: Qn, preset, en
  D_Flip_Flop d_ff_11 (.clk(and_1_out), .D(d_ff_14_q), .Q(ParallelOutput[6]), .reset(Reset));  // open: Qn, preset, en
  D_Flip_Flop d_ff_12 (.clk(and_1_out), .D(d_ff_13_q), .Q(ParallelOutput[5]), .reset(Reset));  // open: Qn, preset, en
  D_Flip_Flop d_ff_13 (.clk(Clock), .D(d_ff_10_q), .Q(d_ff_13_q), .reset(Reset));  // open: Qn, preset, en
  D_Flip_Flop d_ff_14 (.clk(Clock), .D(d_ff_13_q), .Q(d_ff_14_q), .reset(Reset));  // open: Qn, preset, en
  D_Flip_Flop d_ff_15 (.clk(and_1_out), .D(d_ff_16_q), .Q(ParallelOutput[7]), .reset(Reset));  // open: Qn, preset, en
  D_Flip_Flop d_ff_16 (.clk(Clock), .D(d_ff_14_q), .Q(d_ff_16_q), .reset(Reset));  // open: Qn, preset, en
  D_Flip_Flop d_ff_17 (.clk(Latch), .D(d_ff_18_q), .Q(ReadWrite), .reset(Reset));  // open: Qn, preset, en
  D_Flip_Flop d_ff_18 (.clk(Clock), .D(d_ff_16_q), .Q(d_ff_18_q), .reset(Reset));  // open: Qn, preset, en
endmodule

module PISO (
  input  Reset,
  input  Clock,
  input  Latch,
  output SerialOutput,
  output [7:0] EncTime,
  output [7:0] EncValue
);
endmodule

// SPI\nCon.
module SPIController (
  input  Reset,
  input  SPICLK,
  input  SPISS,
  input  SPIMOSI,
  input  [7:0] ENCTime,
  input  [7:0] ENCVal,
  output [7:0] PWMCompareMatch,
  output SPIMSIO
);

  wire and_1_out, and_2_out, not_1_out, not_2_out, pulser_1_output, pulser_2_output, sipo_1_readwrite;

  and and_1 (and_1_out, SPICLK, not_1_out);
  not not_1 (not_1_out, SPISS);
  Pulser pulser_1 (.Input(SPISS), .Output(pulser_1_output));
  not not_2 (not_2_out, sipo_1_readwrite);
  and and_2 (and_2_out, not_1_out, not_2_out);
  Pulser pulser_2 (.Input(and_2_out), .Output(pulser_2_output));
  SIPO sipo_1 (
    .Reset(Reset), .Clock(and_1_out), .Latch(pulser_1_output), .SerialInput(SPIMOSI),
    .ParallelOutput(PWMCompareMatch), .ReadWrite(sipo_1_readwrite));
  PISO piso_1 (
    .Reset(Reset), .Clock(and_1_out), .Latch(pulser_2_output), .SerialOutput(SPIMSIO), .EncTime(ENCTime),
    .EncValue(ENCVal));
endmodule

module MotorController (
  input  Reset,
  input  Clock,
  input  SPICLK,
  input  SPISS,
  input  SPIMOSI,
  input  [1:0] ENCInput,
  output [1:0] PWMOutput,
  output SPIMISO
);

  wire [7:0] enccontroller_1_enctime, enccontroller_1_encval, spicontroller_1_pwmcomparematch;

  SPIController spicontroller_1 (
    .Reset(Reset), .SPICLK(SPICLK), .SPISS(SPISS), .SPIMOSI(SPIMOSI), .SPIMSIO(SPIMISO),
    .PWMCompareMatch(spicontroller_1_pwmcomparematch), .ENCTime(enccontroller_1_encval),
    .ENCVal(enccontroller_1_enctime));
  PWMController pwmcontroller_1 (
    .Reset(Reset), .Clock(Clock), .PWMCompareMatch(spicontroller_1_pwmcomparematch), .PWMOutput(PWMOutput));
  ENCController enccontroller_1 (
    .Reset(Clock), .ENCClock(Reset), .ENCTime(enccontroller_1_enctime), .ENCVal(enccontroller_1_encval),
    .ENCInput(ENCInput));
endmodule

module FPGA (
  input  Reset,
  input  Clock,
  input  SPI0CLK,
  input  SPI0SS,
  input  SPI0MOSI,
  input  [1:0] ENCInput0,
  input  SPI1CLK,
  input  SPI1SS,
  input  SPI1MOSI,
  input  [1:0] ENCInput1,
  input  SW_1,
  input  SW_0,
  input  SW_2,
  output [1:0] PWMOutput0,
  output PWMEN0,
  output SPI0MISO,
  output [1:0] PWMOutput1,
  output PWMEN1,
  output SPI1MISO
);

  nor nor_1 (PWMEN1, SW_1, SW_0);
  MotorController motorcontroller_1 (
    .Reset(Reset), .Clock(Clock), .SPICLK(SPI0CLK), .SPISS(SPI0SS), .SPIMOSI(SPI0MOSI), .SPIMISO(SPI0MISO),
    .PWMOutput(PWMOutput0), .ENCInput(ENCInput0));
  MotorController motorcontroller_2 (
    .Reset(Reset), .Clock(Clock), .SPICLK(SPI1CLK), .SPISS(SPI1SS), .SPIMOSI(SPI1MOSI), .SPIMISO(SPI1MISO),
    .PWMOutput(PWMOutput1), .ENCInput(ENCInput1));
  nor nor_2 (PWMEN0, SW_0, SW_2);
endmodule
